# Fritzing sketch schematic-rx (saved by Fritzing 0.9.1b)

parts:
  C3 = Electrolytic Capacitor [capacitance=10µF package="100 mil [THT, electrolytic]"]
  C2 = Electrolytic Capacitor [capacitance=10µF package="100 mil [THT, electrolytic]"]
  OA1 = Dual Op-Amp [package=dip08]
  P1 = S1133 Si Photodiode [package="8mm Ceramic [THT]"]
  C1 = Electrolytic Capacitor [capacitance=180pF package="100 mil [THT, electrolytic]"]
  R1 = Resistor [tolerance=±5% resistance=47k package=THT]
  USRP = SMA Antenna Connector [package=sma-edge]
  R3 = Resistor [tolerance=±5% resistance=330 package=THT]

nets:
  -5V: C3.-, OA1.A_V-, P1.cathode
  GND: C3.+, C2.-, OA1.A_+IN, USRP.GND
  5V: C2.+, OA1.A_V+
  N1: OA1.A_OUT, C1.+, R1.Pin_1, R3.Pin_0
  N2: OA1.A_-IN, P1.anode, C1.-, R1.Pin_0
  N3: USRP.SIGNAL, R3.Pin_1

// code stored in the sketch: breadboard-tx.fzz.ino

