# Fritzing sketch schematic-tx (saved by Fritzing 0.9.1b)

parts:
  OA1 = Dual Op-Amp [package=dip08]
  R3 = Resistor [tolerance=±5% resistance=470k package=THT]
  R4 = Resistor [tolerance=±5% resistance=470 package=THT]
  Q1 = Basic FET N-Channel [package="TO220 [THT]"]
  C1 = Electrolytic Capacitor [capacitance=470µF package="100 mil [THT, electrolytic]"]
  C2 = Electrolytic Capacitor [capacitance=10µF package="100 mil [THT, electrolytic]"]
  C3 = Electrolytic Capacitor [capacitance=10µF package="100 mil [THT, electrolytic]"]
  R2 = Resistor [tolerance=±5% resistance=470 package=THT]
  R1 = Resistor [tolerance=±5% resistance=47k package=THT]
  D1 = LEDs [package=led10mm]
  USRP = SMA Antenna Connector [package=sma-edge]

nets:
  N1: OA1.A_OUT, R3.Pin_0, Q1.gate
  N2: OA1.A_-IN, R3.Pin_1, R1.Pin_0
  N3: OA1.A_+IN, C1.-, R2.Pin_0
  -5V: OA1.A_V-, C3.-
  5V: OA1.A_V+, R4.Pin_0, C2.+
  N4: R4.Pin_1, D1.A
  N5: Q1.drain, D1.C
  GND: Q1.source, C2.-, C3.+, R2.Pin_1, R1.Pin_1, USRP.GND
  N6: C1.+, USRP.SIGNAL
